# Fritzing sketch Sketch (saved by Fritzing 0.9.3b)
breadboards: 1

parts:
  Част1 = Arduino Uno (Rev3)
  R1 = Trimmer Potentiometer [maximum_resistance=10kΩ package=THT]
  R2 = Trimmer Potentiometer [maximum_resistance=10kΩ package=THT]
  R3 = Trimmer Potentiometer [maximum_resistance=10kΩ package=THT]

nets:
  N1: Част1.A1, R1.wiper
  N2: Част1.A2, R2.wiper
  N3: Част1.A3, R3.wiper
  N4: Част1.GND, R1.leg1, R2.leg1, R3.leg1
  N5: Част1.5V, R1.leg2, R2.leg2, R3.leg2

// code stored in the sketch: Sketch.ino
#define R A1
#define G A2
#define B A3
#define L A4

int r, g, b;

void setup() {  
  Serial.begin(9600);
}

void loop() {
  int oldr = r, oldg = g, oldb = b;
  r = map(analogRead(R), 0, 1023, 0, 255);
  g = map(analogRead(G), 0, 1023, 0, 255);
  b = map(analogRead(B), 0, 1023, 0, 255);

  if (oldr == r && oldg == g && oldb == b) {
    return;
  }

  Serial.write(r);
  Serial.write(g);
  Serial.write(b);
  Serial.flush();
    
  delay(100);
}
